# Fritzing sketch alarm_clock (saved by Fritzing 0.9.3b)
breadboards: 1

parts:
  TFT1 = 2.2" TFT with MicroSD Breakout  # not connected
  J1 = longpad pin header, 13 pins [form="long pad"]
  J2 = Piezo Speaker
  Part1 = Arduino Uno (Rev3)
  Part3 = Adafruit DS1307 RTC Breakout [part_number="Adafruit #264"]
  Matrix_keypad1 = KEYPAD 4x4

nets:
  5V: J1.pin1, Part1.5V, Part3.VCC
  GND: J1.pin2, J2.pin1, Part1.GND, Part3.GND
  N1: J1.pin3, Part1.D13/SCK
  N2: J1.pin4, Part1.D11_PWM/MOSI
  N3: J1.pin5, Part1.D9_PWM
  N4: J1.pin6, Part1.D8
  N5: J1.pin7, Part1.D10_PWM/SS
  N6: J2.pin2, Part1.D7
  N7: Part1.A0, Matrix_keypad1.row1
  N8: Part1.A1, Matrix_keypad1.row2
  N9: Part1.A2, Matrix_keypad1.row3
  N10: Part1.A3, Matrix_keypad1.row4
  N11: Part1.A4/SDA, Part3.SDA
  N12: Part1.A5/SCL, Part3.SCL
  N13: Part1.D2, Matrix_keypad1.col4
  N14: Part1.D3_PWM, Matrix_keypad1.col3
  N15: Part1.D4, Matrix_keypad1.col2
  N16: Part1.D5_PWM, Matrix_keypad1.col1

custom parts:
  2.2" TFT with MicroSD Breakout: 2.2" TFT Display with HX8340B Controller and MicroSD Card
  Adafruit DS1307 RTC Breakout: This is a great battery-backed real time clock (RTC) that allows your microcontroller project to keep track of time even if it is reprogrammed, or if the power is lost. Perfect for datalogging, clock-building, time stamping, timers and alarms, etc. The DS1307 is the most popular RTC - but it requires 5V power to work (although we've used it with 5V power and 3.3V logic successfully) PCB &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
  KEYPAD 4x4: Matrix keypad 16 buttons, 4 rows x 4 columns
